// Logisim project organ16.circ as structural Verilog: 10 circuits, main circuit main
module main (
);

  wire and_1_out, and_2_out, and_3_out, and_4_out, button_1_out, clock_1_out, CLOCK_SIGNAL, comparator_1_eq,
       comparator_2_eq, comparator_3_eq, comparator_4_eq, comparator_4_gt, comparator_5_lt, comparator_6_eq,
       cpu_1_halt, cpu_1_ram_clock, cpu_1_write_to_ram, IO_IN_OUT, multiplexer_2_out, multiplexer_3_out,
       or_1_out, or_2_out, or_3_out, or_4_out, RESET, rgb_video_1_p2;
  wire [1:0] cpu_1_ram_adress_3, IO_PORT;
  wire [6:0] cpu_1_ram_adress, cpu_1_ram_adress_2, dipswitch_3_sw16, divider_1_rem, multiplexer_6_out;
  wire [15:0] cpu_1_ram_data, dipswitch_1_sw16, dipswitch_2_sw16, IO_DATA_OUT, IO_PORT_A_p3, IO_PORT_B_p3,
       IO_PORT_C_p3, multiplexer_1_out, multiplexer_4_out, multiplexer_5_out, RAM_1Mbit_dout;

  Button RESET_SYSTEM (.out(RESET));
  Multiplexer #(.select(2), .width(16)) multiplexer_1 (
    .in0(IO_PORT_A_p3), .in1(IO_PORT_B_p3), .in2(IO_PORT_C_p3), .out(multiplexer_1_out), .sel(IO_PORT));  // open: in3
  Comparator #(.width(2)) comparator_1 (.a(IO_PORT), .b(2'b00), .eq(comparator_1_eq));  // open: gt, lt
  Comparator #(.width(2)) comparator_2 (.a(IO_PORT), .b(2'b01), .eq(comparator_2_eq));  // open: gt, lt
  Comparator #(.width(2)) comparator_3 (.a(IO_PORT), .b(2'b10), .eq(comparator_3_eq));  // open: gt, lt
  and and_1 (and_1_out, IO_IN_OUT, comparator_1_eq);
  and and_2 (and_2_out, IO_IN_OUT, comparator_2_eq);
  and and_3 (and_3_out, IO_IN_OUT, comparator_3_eq);
  CPU cpu_1 (
    .IO_DATA_IN(multiplexer_1_out), .RAM_OUT(RAM_1Mbit_dout), .CLOCK_SIGNAL(CLOCK_SIGNAL),
    .GLOBAL_RESET(RESET), .HALT(cpu_1_halt),
    .RAM_ADRESS({cpu_1_ram_adress_3, cpu_1_ram_adress_2, cpu_1_ram_adress}),
    .WRITE_TO_RAM(cpu_1_write_to_ram), .RAM_CLOCK(cpu_1_ram_clock), .RAM_DATA(cpu_1_ram_data),
    .IO_PORT(IO_PORT), .IO_DATA_OUT(IO_DATA_OUT), .IO_IN_OUT(IO_IN_OUT));
  or or_1 (or_1_out, and_1_out, RESET);
  or or_2 (or_2_out, and_2_out, RESET);
  or or_3 (or_3_out, and_3_out, RESET);
  // PortIO #(.number(16)) IO_PORT_A: pin names not known; wires that end beside it: or_1_out, IO_DATA_OUT, IO_PORT_A_p3
  // PortIO #(.number(16)) IO_PORT_B: pin names not known; wires that end beside it: or_2_out, IO_DATA_OUT, IO_PORT_B_p3
  // PortIO #(.number(16)) IO_PORT_C: pin names not known; wires that end beside it: or_3_out, IO_DATA_OUT, IO_PORT_C_p3
  Clock clock_1 (.out(clock_1_out));
  DipSwitch #(.number(16)) dipswitch_1 (
    .sw1(dipswitch_1_sw16[15]), .sw2(dipswitch_1_sw16[14]), .sw3(dipswitch_1_sw16[13]),
    .sw4(dipswitch_1_sw16[12]), .sw5(dipswitch_1_sw16[11]), .sw6(dipswitch_1_sw16[10]),
    .sw7(dipswitch_1_sw16[9]), .sw8(dipswitch_1_sw16[8]), .sw9(dipswitch_1_sw16[7]),
    .sw10(dipswitch_1_sw16[6]), .sw11(dipswitch_1_sw16[5]), .sw12(dipswitch_1_sw16[4]),
    .sw13(dipswitch_1_sw16[3]), .sw14(dipswitch_1_sw16[2]), .sw15(dipswitch_1_sw16[1]),
    .sw16(dipswitch_1_sw16[0]));
  Multiplexer multiplexer_2 (.in0(cpu_1_write_to_ram), .in1(1'b1), .out(multiplexer_2_out), .sel(button_1_out));
  DipSwitch #(.number(16)) dipswitch_2 (
    .sw1(dipswitch_2_sw16[15]), .sw2(dipswitch_2_sw16[14]), .sw3(dipswitch_2_sw16[13]),
    .sw4(dipswitch_2_sw16[12]), .sw5(dipswitch_2_sw16[11]), .sw6(dipswitch_2_sw16[10]),
    .sw7(dipswitch_2_sw16[9]), .sw8(dipswitch_2_sw16[8]), .sw9(dipswitch_2_sw16[7]),
    .sw10(dipswitch_2_sw16[6]), .sw11(dipswitch_2_sw16[5]), .sw12(dipswitch_2_sw16[4]),
    .sw13(dipswitch_2_sw16[3]), .sw14(dipswitch_2_sw16[2]), .sw15(dipswitch_2_sw16[1]),
    .sw16(dipswitch_2_sw16[0]));
  Comparator #(.mode("unsigned"), .width(16)) comparator_4 (
    .a({cpu_1_ram_adress_3, cpu_1_ram_adress_2, cpu_1_ram_adress}), .b(16'h8000), .gt(comparator_4_gt),
    .eq(comparator_4_eq));  // open: lt
  Comparator #(.mode("unsigned"), .width(16)) comparator_5 (
    .a({cpu_1_ram_adress_3, cpu_1_ram_adress_2, cpu_1_ram_adress}), .b(16'hc000), .lt(comparator_5_lt));  // open: gt, eq
  Multiplexer multiplexer_3 (.in0(cpu_1_ram_clock), .in1(1'b1), .out(multiplexer_3_out), .sel(button_1_out));
  or or_4 (or_4_out, comparator_4_gt, comparator_4_eq);
  and and_4 (and_4_out, or_4_out, comparator_5_lt);
  CLCK MAIN_CLOCK (.CLOCK_SIGNAL(clock_1_out), .HALT(cpu_1_halt), .OUTPUT_SIGNAL(CLOCK_SIGNAL));
  Button button_1 (.out(button_1_out));
  Multiplexer #(.width(16)) multiplexer_4 (
    .in0({cpu_1_ram_adress_3, cpu_1_ram_adress_2, cpu_1_ram_adress}), .in1(dipswitch_1_sw16),
    .out(multiplexer_4_out), .sel(button_1_out));
  Multiplexer #(.width(16)) multiplexer_5 (
    .in0(cpu_1_ram_data), .in1(dipswitch_2_sw16), .out(multiplexer_5_out), .sel(button_1_out));
  // Probe on {cpu_1_ram_adress_3, cpu_1_ram_adress_2, cpu_1_ram_adress}
  DipSwitch #(.number(16)) dipswitch_3 (
    .sw10(dipswitch_3_sw16[6]), .sw11(dipswitch_3_sw16[5]), .sw12(dipswitch_3_sw16[4]),
    .sw13(dipswitch_3_sw16[3]), .sw14(dipswitch_3_sw16[2]), .sw15(dipswitch_3_sw16[1]),
    .sw16(dipswitch_3_sw16[0]));  // open: sw1, sw2, sw3, sw4, sw5, sw6, sw7, sw8, sw9
  RAM #(.addrWidth(16), .clearpin("true"), .dataWidth(16), .enables("line"), .\type ("nonvolatile")) RAM_1Mbit (
    .addr(multiplexer_4_out), .we(multiplexer_2_out), .clk(multiplexer_3_out), .din(multiplexer_5_out),
    .dout(RAM_1Mbit_dout), .clr(RESET));
  Divider #(.width(7)) divider_1 (.a(cpu_1_ram_adress), .b(dipswitch_3_sw16), .rem(divider_1_rem));  // open: out, upper
  Comparator #(.mode("unsigned"), .width(7)) comparator_6 (
    .a(cpu_1_ram_adress), .b(dipswitch_3_sw16), .eq(comparator_6_eq));  // open: gt, lt
  Multiplexer #(.width(7)) multiplexer_6 (
    .in0(divider_1_rem), .in1(dipswitch_3_sw16), .out(multiplexer_6_out), .sel(comparator_6_eq));
  // RGB_Video #(.cursor("No Cursor")) rgb_video_1: pin names not known; wires that end beside it: RESET, rgb_video_1_p2, and_4_out, multiplexer_6_out, cpu_1_ram_adress_2, multiplexer_5_out
  not not_1 (rgb_video_1_p2, CLOCK_SIGNAL);

  // Notes on the sheet:
  //   ADDRESS
  //   DATA
  //   WRITE
  //   ORGAN-16 v.0.8.2
  //   USER I/O (COMPUTER)
  //   DON'T FORGET TO PUT THAT AT : 0x7F
  //   (screen's width)
  //   NOTE : MOST MODERN PARALLEL 64Kx16
  //   SRAMs AREN'T ASYNCHRONOUS,
  //    SO TO IMPLEMENT THE PROCESSOR IRL,
  //   THE RAM NEEDS A LITTLE BIT OF TWEAKING
endmodule

module CPU (
  input  [15:0] IO_DATA_IN,
  input  [15:0] RAM_OUT,
  input  CLOCK_SIGNAL,
  input  GLOBAL_RESET,
  output HALT,
  output [15:0] RAM_ADRESS,
  output WRITE_TO_RAM,
  output RAM_CLOCK,
  output [15:0] RAM_DATA,
  output [1:0] IO_PORT,
  output [15:0] IO_DATA_OUT,
  output IO_IN_OUT
);

  wire and_1_out, and_2_out, and_3_out, and_5_out, and_9_out, and_12_out, and_13_out, and_14_out, and_15_out,
       and_16_out, and_17_out, ContainsAddress, CONTROL_UNIT_1_containsaddress, CONTROL_UNIT_1_isnextext,
       CONTROL_UNIT_1_jsr, CONTROL_UNIT_1_memwrite, CONTROL_UNIT_1_pc_load, CONTROL_UNIT_1_reg_is_adr,
       CONTROL_UNIT_1_regwrite, CONTROL_UNIT_1_sp_change, d_ff_1_q, ENABLE_ALU, FLAGS_WRITE, IS_CURR_ADR,
       IS_CURR_ADR_BASE, IS_CURR_ADR_JSR, IS_CURR_EXT, IS_CURR_JSR, IS_CURR_RTS, IS_CURR_SP_CHANGE,
       IS_NEXT_EXT, JSR, MAIN_ALU_flag_carry, MAIN_ALU_flag_negative, MAIN_ALU_flag_overflow,
       MAIN_ALU_flag_zero, MEM_TO_REG, MEM_WRITE, multiplexer_6_out, multiplexer_11_out, multiplexer_13_out,
       not_1_out, not_2_out, not_3_out, not_4_out, not_5_out, not_6_out, not_7_out, not_8_out, not_9_out,
       not_10_out, not_11_out, not_12_out, not_13_out, not_14_out, not_15_out, not_16_out, not_17_out,
       not_18_out, not_19_out, not_20_out, not_21_out, not_22_out, not_23_out, not_24_out, not_25_out,
       not_26_out, or_1_out, or_2_out, or_3_out, or_5_out, or_7_out, or_8_out, or_10_out, PC_LOAD,
       REG_IS_ADR, REG_IS_CURR_ADR, REG_WRITE, RTS, SP_CHANGE, SP_POP, USE_IN;
  wire [2:0] DST_REG, SRC_REGA, SRC_REGB;
  wire [3:0] ALU_OPCODE, FLAGS;
  wire [15:0] adder_1_out, adder_2_out, DATA_RB, demultiplexer_1_out0, demultiplexer_1_out1,
       INSTRUCTION_REG_MAIN_1_data_out, IR_EXT_DATA, MAIN_ALU_result, multiplexer_1_out, multiplexer_2_out,
       multiplexer_7_out, multiplexer_8_out, multiplexer_9_out, multiplexer_10_out, multiplexer_12_out,
       PROG_COUNTER, register_1_q, STACK_POINTER, subtractor_1_out;

  Demultiplexer #(.width(16)) demultiplexer_1 (
    .out0(demultiplexer_1_out0), .out1(demultiplexer_1_out1), .in(RAM_OUT), .sel(IS_CURR_EXT));
  Register #(.width(16)) register_1 (.D(IR_EXT_DATA), .en(1'b1), .clk(not_1_out), .Q(register_1_q), .clr(GLOBAL_RESET));
  not not_1 (not_1_out, CLOCK_SIGNAL);
  // Probe on demultiplexer_1_out0
  or or_1 (or_1_out, CLOCK_SIGNAL, IS_CURR_EXT, REG_IS_CURR_ADR);
  not not_2 (not_2_out, IS_CURR_SP_CHANGE);
  not not_3 (not_3_out, or_1_out);
  Multiplexer #(.width(16)) multiplexer_1 (
    .in0(register_1_q), .in1(DATA_RB), .out(multiplexer_1_out), .sel(REG_IS_CURR_ADR));
  not not_4 (not_4_out, IS_CURR_JSR);
  not not_5 (not_5_out, PC_LOAD);
  INSTRUCTION_REG_MAIN INSTRUCTION_REG_MAIN_1 (
    .DATA_IN(demultiplexer_1_out0), .ENABLE(not_2_out), .CLOCK(not_3_out), .RESET(GLOBAL_RESET),
    .DATA_OUT(INSTRUCTION_REG_MAIN_1_data_out));
  INSTRUCTION_REG_EXT INSTRUCTION_REG_EXT_1 (
    .DATA_IN(demultiplexer_1_out1), .ENABLE(1'b1), .CLOCK(IS_CURR_EXT), .RESET(GLOBAL_RESET),
    .DATA_OUT(IR_EXT_DATA));
  Multiplexer #(.width(16)) multiplexer_2 (
    .in0(multiplexer_1_out), .in1(STACK_POINTER), .out(multiplexer_2_out), .sel(IS_CURR_SP_CHANGE));
  and and_1 (and_1_out, not_4_out, IS_CURR_ADR, IS_CURR_EXT, not_5_out);
  // Probe on IR_EXT_DATA
  or or_2 (or_2_out, and_1_out, IS_CURR_SP_CHANGE, REG_IS_CURR_ADR);
  // Probe on INSTRUCTION_REG_MAIN_1_data_out
  // Probe on INSTRUCTION_REG_MAIN_1_data_out
  Multiplexer #(.width(16)) multiplexer_3 (
    .in0(PROG_COUNTER), .in1(multiplexer_2_out), .out(RAM_ADRESS), .sel(or_2_out));
  Adder #(.width(16)) adder_1 (.a(PROG_COUNTER), .b(16'h2), .out(adder_1_out));  // open: cin, cout
  not not_6 (not_6_out, CLOCK_SIGNAL);
  Multiplexer multiplexer_4 (.in0(CLOCK_SIGNAL), .in1(not_6_out), .out(RAM_CLOCK), .sel(IS_CURR_SP_CHANGE));
  Multiplexer #(.width(16)) multiplexer_5 (.in0(IO_DATA_OUT), .in1(adder_1_out), .out(RAM_DATA), .sel(IS_CURR_JSR));
  ALU MAIN_ALU (
    .A(IO_DATA_OUT), .B(DATA_RB), .ALUOpCode(ALU_OPCODE), .ALU_Enable(ENABLE_ALU), .RESULT(MAIN_ALU_result),
    .FLAG_ZERO(MAIN_ALU_flag_zero), .FLAG_NEGATIVE(MAIN_ALU_flag_negative), .FLAG_CARRY(MAIN_ALU_flag_carry),
    .FLAG_OVERFLOW(MAIN_ALU_flag_overflow));
  Multiplexer multiplexer_6 (.in0(and_5_out), .in1(1'b0), .out(multiplexer_6_out), .sel(IS_CURR_EXT));
  not not_7 (not_7_out, CLOCK_SIGNAL);
  D_Flip_Flop d_ff_1 (.D(multiplexer_6_out), .clk(not_7_out), .Q(d_ff_1_q), .reset(GLOBAL_RESET));  // open: Qn, preset
  Subtractor #(.width(16)) subtractor_1 (.a(STACK_POINTER), .b(16'h1), .out(subtractor_1_out));  // open: bin, bout
  Adder #(.width(16)) adder_2 (.a(STACK_POINTER), .b(16'h1), .out(adder_2_out));  // open: cin, cout
  not not_8 (not_8_out, CLOCK_SIGNAL);
  CONTROL_UNIT CONTROL_UNIT_1 (
    .OpCode(INSTRUCTION_REG_MAIN_1_data_out[15:13]), .SubOpCode(INSTRUCTION_REG_MAIN_1_data_out[12:9]),
    .OpData(INSTRUCTION_REG_MAIN_1_data_out[8:0]), .FLAGS(FLAGS), .ALU_Data({ENABLE_ALU, ALU_OPCODE}),
    .RegWrite(CONTROL_UNIT_1_regwrite), .SrcRB(SRC_REGB), .SrcRA(SRC_REGA), .DstR(DST_REG),
    .IsNextExt(CONTROL_UNIT_1_isnextext), .FlagsWrite(FLAGS_WRITE), .MemWrite(CONTROL_UNIT_1_memwrite),
    .MemToReg(MEM_TO_REG), .ContainsAddress(CONTROL_UNIT_1_containsaddress),
    .PC_Load(CONTROL_UNIT_1_pc_load), .SP_POP(SP_POP), .SP_CHANGE(CONTROL_UNIT_1_sp_change),
    .JSR(CONTROL_UNIT_1_jsr), .RTS(RTS), .REG_IS_ADR(CONTROL_UNIT_1_reg_is_adr), .HALT(HALT),
    .USE_IN(USE_IN), .USE_OUT(IO_IN_OUT), .IO_PORT(IO_PORT));
  or or_3 (or_3_out, MEM_WRITE, IS_CURR_JSR);
  Multiplexer #(.width(16)) multiplexer_7 (
    .in0(subtractor_1_out), .in1(adder_2_out), .out(multiplexer_7_out), .sel(SP_POP));
  and and_2 (and_2_out, IS_CURR_SP_CHANGE, not_8_out);
  FLAGS_REG FLAGS_REG_1 (
    .IN_Z(MAIN_ALU_flag_zero), .IN_N(MAIN_ALU_flag_negative), .IN_C(MAIN_ALU_flag_carry),
    .IN_O(MAIN_ALU_flag_overflow), .ENABLE(FLAGS_WRITE), .CLOCK(CLOCK_SIGNAL), .RESET(GLOBAL_RESET),
    .OUT_DATA(FLAGS));
  not not_9 (not_9_out, d_ff_1_q);
  Register #(.width(16)) u_STACK_POINTER (
    .D(multiplexer_7_out), .en(1'b1), .clk(and_2_out), .Q(STACK_POINTER));  // open: clr
  not not_10 (not_10_out, IS_CURR_JSR);
  and and_3 (and_3_out, REG_IS_CURR_ADR, not_11_out);
  not not_11 (not_11_out, REG_WRITE);
  // Probe on STACK_POINTER
  and and_4 (JSR, CONTROL_UNIT_1_jsr, not_10_out);
  // Probe on RAM_OUT
  and and_5 (and_5_out, or_3_out, not_9_out);
  not not_12 (not_12_out, IS_CURR_EXT);
  and and_6 (REG_IS_ADR, CONTROL_UNIT_1_reg_is_adr, not_13_out);
  not not_13 (not_13_out, REG_IS_CURR_ADR);
  or or_4 (WRITE_TO_RAM, and_3_out, and_5_out);
  or or_5 (or_5_out, IS_CURR_EXT, ENABLE_ALU, REG_IS_CURR_ADR, USE_IN);
  and and_7 (IS_NEXT_EXT, CONTROL_UNIT_1_isnextext, not_12_out);
  not not_14 (not_14_out, IS_CURR_SP_CHANGE);
  not not_15 (not_15_out, IS_CURR_EXT);
  and and_8 (REG_WRITE, CONTROL_UNIT_1_regwrite, or_5_out);
  and and_9 (and_9_out, CONTROL_UNIT_1_containsaddress, IS_CURR_EXT);
  and and_10 (SP_CHANGE, CONTROL_UNIT_1_sp_change, not_14_out, not_15_out);
  Multiplexer #(.enable("true"), .width(16)) multiplexer_8 (
    .in0(MAIN_ALU_result), .in1(IR_EXT_DATA), .out(multiplexer_8_out), .sel(IS_CURR_EXT), .en(REG_WRITE));
  or or_6 (ContainsAddress, JSR, and_9_out);
  or or_7 (or_7_out, IS_CURR_SP_CHANGE, REG_IS_CURR_ADR);
  or or_8 (or_8_out, IS_CURR_EXT, REG_IS_CURR_ADR);
  and and_11 (PC_LOAD, CONTROL_UNIT_1_pc_load, IS_CURR_EXT);
  Multiplexer #(.width(16)) multiplexer_9 (
    .in0(multiplexer_8_out), .in1(RAM_OUT), .out(multiplexer_9_out), .sel(or_7_out));
  not not_16 (not_16_out, SP_POP);
  and and_12 (and_12_out, CONTROL_UNIT_1_memwrite, or_8_out);
  Multiplexer #(.width(16)) multiplexer_10 (
    .in0(multiplexer_9_out), .in1(IO_DATA_IN), .out(multiplexer_10_out), .sel(USE_IN));
  and and_13 (and_13_out, IS_CURR_SP_CHANGE, not_16_out);
  or or_9 (MEM_WRITE, and_13_out, and_12_out);
  Multiplexer multiplexer_11 (.in0(CLOCK_SIGNAL), .in1(not_17_out), .out(multiplexer_11_out), .sel(IS_CURR_ADR));
  not not_17 (not_17_out, CLOCK_SIGNAL);
  not not_18 (not_18_out, IS_CURR_JSR);
  GENERAL_PURPOSE_REGS GENERAL_PURPOSE_REGS_1 (
    .RB_OUT(SRC_REGB), .RA_OUT(SRC_REGA), .R_WRITE(REG_WRITE), .DATA(multiplexer_10_out),
    .CLOCK(multiplexer_11_out), .R_IN(DST_REG), .RESET(GLOBAL_RESET), .DATA_RA_OUT(IO_DATA_OUT),
    .DATA_RB_OUT(DATA_RB));
  and and_14 (and_14_out, PC_LOAD, not_18_out, IS_CURR_ADR);
  not not_19 (not_19_out, IS_CURR_JSR);
  not not_20 (not_20_out, IS_CURR_SP_CHANGE);
  not not_21 (not_21_out, SP_CHANGE);
  not not_22 (not_22_out, REG_IS_CURR_ADR);
  not not_23 (not_23_out, REG_IS_ADR);
  or or_10 (or_10_out, and_14_out, RTS);
  and and_15 (and_15_out, CLOCK_SIGNAL, not_19_out, not_20_out, not_21_out, not_22_out, not_23_out);
  Multiplexer #(.width(16)) multiplexer_12 (.in0(IR_EXT_DATA), .in1(RAM_OUT), .out(multiplexer_12_out), .sel(RTS));
  PROGRAM_COUNTER PROGRAM_COUNTER_MAIN (
    .PC_DATA(multiplexer_12_out), .PC_Load(or_10_out), .CLOCK(and_15_out), .RESET(GLOBAL_RESET),
    .PC_Out(PROG_COUNTER));
  // Probe on PROG_COUNTER
  and and_16 (and_16_out, ContainsAddress, not_24_out);
  not not_24 (not_24_out, JSR);
  Multiplexer multiplexer_13 (.in0(IS_NEXT_EXT), .in1(1'b1), .out(multiplexer_13_out), .sel(IS_CURR_JSR));
  D_Flip_Flop CURRENT_IS_ADDR_BASE (
    .D(and_16_out), .clk(not_25_out), .Q(IS_CURR_ADR_BASE), .reset(GLOBAL_RESET));  // open: Qn, preset
  not not_25 (not_25_out, CLOCK_SIGNAL);
  D_Flip_Flop CURRENT_IS_ADDR_JSR (
    .D(ContainsAddress), .clk(CLOCK_SIGNAL), .Q(IS_CURR_ADR_JSR), .reset(GLOBAL_RESET));  // open: Qn, preset
  and and_17 (and_17_out, JSR, not_26_out);
  not not_26 (not_26_out, IS_CURR_EXT);
  D_Flip_Flop CURRENT_IS_EXT (
    .D(multiplexer_13_out), .clk(CLOCK_SIGNAL), .Q(IS_CURR_EXT), .reset(GLOBAL_RESET));  // open: Qn, preset
  D_Flip_Flop CURRENT_CHANGES_SP (
    .D(SP_CHANGE), .clk(CLOCK_SIGNAL), .Q(IS_CURR_SP_CHANGE), .reset(GLOBAL_RESET));  // open: Qn, preset
  D_Flip_Flop CURRENTLY_JSR (
    .D(and_17_out), .clk(CLOCK_SIGNAL), .Q(IS_CURR_JSR), .reset(GLOBAL_RESET));  // open: Qn, preset
  D_Flip_Flop CURRENTLY_RTS (.D(RTS), .clk(CLOCK_SIGNAL), .Q(IS_CURR_RTS), .reset(GLOBAL_RESET));  // open: Qn, preset
  D_Flip_Flop REG_IS_CURR_ADDR (
    .D(REG_IS_ADR), .clk(CLOCK_SIGNAL), .Q(REG_IS_CURR_ADR), .reset(GLOBAL_RESET));  // open: Qn, preset
  or or_11 (IS_CURR_ADR, IS_CURR_ADR_BASE, IS_CURR_ADR_JSR);

  // Other names for the same wires on the sheet: DATA_RA[15:0] = IO_DATA_OUT; USE_OUT = IO_IN_OUT

  // Notes on the sheet:
  //   INSTRUCTIONS REGs
  //   MEMORY INTERFACE
  //   ALU + FLAGS REG
  //   STACK POINTER
  //   CONTROL UNIT
  //   GENERAL PURPOSE REGs
  //   PROGRAM COUNTER
  //   TEMPORARY VALUES
endmodule

module ALU (
  input  [15:0] A,
  input  [15:0] B,
  input  [3:0] ALUOpCode,
  input  ALU_Enable,
  output [15:0] RESULT,
  output FLAG_ZERO,
  output FLAG_NEGATIVE,
  output FLAG_CARRY,
  output FLAG_OVERFLOW
);

  wire adder_1_cout, and_2_out, and_3_out, nor_2_out, subtractor_1_bout, xnor_1_out, xor_2_out, xor_3_out,
       xor_4_out;
  wire [15:0] adder_1_out, and_1_out, divider_1_out, divider_2_rem, multiplier_1_out, nand_1_out, nor_1_out,
       not_1_out, or_1_out, subtractor_1_out, subtractor_2_out, xor_1_out;

  Adder #(.width(16)) adder_1 (.a(A), .b(B), .out(adder_1_out), .cout(adder_1_cout));  // open: cin
  Subtractor #(.width(16)) subtractor_1 (.a(A), .b(B), .out(subtractor_1_out), .bout(subtractor_1_bout));  // open: bin
  Multiplier #(.width(16)) multiplier_1 (.a(A), .b(B), .out(multiplier_1_out));  // open: cin, cout
  Divider #(.width(16)) divider_1 (.a(A), .b(B), .out(divider_1_out));  // open: upper, rem
  Divider #(.width(16)) divider_2 (.a(A), .b(B), .rem(divider_2_rem));  // open: out, upper
  assign and_1_out = A & B;  // AND_Gate and_1, 16 bits wide
  assign or_1_out = A | B;  // OR_Gate or_1, 16 bits wide
  assign nand_1_out = ~(A & B);  // NAND_Gate nand_1, 16 bits wide
  assign nor_1_out = ~(A | B);  // NOR_Gate nor_1, 16 bits wide
  assign xor_1_out = A ^ B;  // XOR_Gate xor_1, 16 bits wide
  Subtractor #(.width(16)) subtractor_2 (.a(A), .b(B), .out(subtractor_2_out));  // open: bin, bout
  assign not_1_out = ~A;  // NOT_Gate not_1, 16 bits wide
  Multiplexer #(.enable("true"), .select(4), .width(16)) multiplexer_1 (
    .in0(adder_1_out), .in1(subtractor_1_out), .in2(multiplier_1_out), .in3(divider_1_out),
    .in4(divider_2_rem), .in5(and_1_out), .in6(or_1_out), .in7(nand_1_out), .in8(nor_1_out), .in9(xor_1_out),
    .in10(subtractor_2_out), .in11(not_1_out), .out(RESULT), .sel(ALUOpCode), .en(ALU_Enable));  // open: in12, in13, in14, in15
  Multiplexer #(.enable("true"), .select(4)) multiplexer_2 (
    .in0(adder_1_cout), .in1(subtractor_1_bout), .in2(1'b0), .in3(1'b0), .in4(1'b0), .in5(1'b0), .in6(1'b0),
    .in7(1'b0), .in8(1'b0), .in9(1'b0), .in10(subtractor_1_bout), .out(FLAG_CARRY), .sel(ALUOpCode),
    .en(ALU_Enable));  // open: in11, in12, in13, in14, in15
  nor nor_2 (nor_2_out, RESULT[0], RESULT[1], RESULT[2], RESULT[3], RESULT[4], RESULT[5], RESULT[6], RESULT[7], RESULT[8], RESULT[9], RESULT[10], RESULT[11], RESULT[12], RESULT[13], RESULT[14], RESULT[15]);
  xor xor_2 (xor_2_out, RESULT[15], A[15]);
  xnor xnor_1 (xnor_1_out, A[15], B[15]);
  xor xor_3 (xor_3_out, RESULT[15], A[15]);
  xor xor_4 (xor_4_out, A[15], B[15]);
  and and_2 (and_2_out, xor_2_out, xnor_1_out);
  and and_3 (and_3_out, xor_3_out, xor_4_out);
  Multiplexer multiplexer_3 (.in0(1'b0), .in1(nor_2_out), .out(FLAG_ZERO), .sel(ALU_Enable));
  Multiplexer multiplexer_4 (.in0(1'b0), .in1(RESULT[15]), .out(FLAG_NEGATIVE), .sel(ALU_Enable));
  Multiplexer #(.enable("true"), .select(4)) multiplexer_5 (
    .in0(and_2_out), .in1(and_3_out), .in2(1'b0), .in3(1'b0), .in4(1'b0), .in5(1'b0), .in6(1'b0), .in7(1'b0),
    .in8(1'b0), .in9(1'b0), .in10(and_3_out), .out(FLAG_OVERFLOW), .sel(ALUOpCode), .en(ALU_Enable));  // open: in11, in12, in13, in14, in15

  // Notes on the sheet:
  //   ADD
  //   SUB
  //   MUL
  //   DIV
  //   MOD
  //   AND
  //   OR
  //   NAND
  //   NOR
  //   XOR
  //   CMP
  //   NOT
endmodule

module CLCK (
  input  CLOCK_SIGNAL,
  input  HALT,
  output OUTPUT_SIGNAL
);

  wire not_1_out;

  not not_1 (not_1_out, HALT);
  and and_1 (OUTPUT_SIGNAL, CLOCK_SIGNAL, not_1_out);
endmodule

module GENERAL_PURPOSE_REGS (
  input  [15:0] DATA,
  input  R_WRITE,
  input  [2:0] R_IN,
  input  CLOCK,
  input  [2:0] RA_OUT,
  input  RESET,
  input  [2:0] RB_OUT,
  output [15:0] DATA_RA_OUT,
  output [15:0] DATA_RB_OUT
);

  wire decoder_1_out0, decoder_1_out1, decoder_1_out2, decoder_1_out3, decoder_1_out4, decoder_1_out5,
       decoder_1_out6, decoder_1_out7, not_1_out, not_2_out, not_3_out, not_4_out, not_5_out, not_6_out,
       not_7_out, not_8_out;
  wire [15:0] R0_q, R1_q, R2_q, R3_q, R4_q, R5_q, R6_q, R7_q;

  // Probe on DATA
  Decoder #(.select(3)) decoder_1 (
    .out0(decoder_1_out0), .out1(decoder_1_out1), .out2(decoder_1_out2), .out3(decoder_1_out3),
    .out4(decoder_1_out4), .out5(decoder_1_out5), .out6(decoder_1_out6), .out7(decoder_1_out7), .sel(R_IN),
    .en(R_WRITE));
  Register #(.width(16)) R0 (.D(DATA), .en(decoder_1_out0), .clk(not_1_out), .Q(R0_q), .clr(RESET));
  not not_1 (not_1_out, CLOCK);
  Register #(.width(16)) R1 (.D(DATA), .en(decoder_1_out1), .clk(not_2_out), .Q(R1_q), .clr(RESET));
  not not_2 (not_2_out, CLOCK);
  Register #(.width(16)) R2 (.D(DATA), .en(decoder_1_out2), .clk(not_3_out), .Q(R2_q), .clr(RESET));
  not not_3 (not_3_out, CLOCK);
  Register #(.width(16)) R3 (.D(DATA), .en(decoder_1_out3), .clk(not_4_out), .Q(R3_q), .clr(RESET));
  not not_4 (not_4_out, CLOCK);
  Register #(.width(16)) R4 (.D(DATA), .en(decoder_1_out4), .clk(not_5_out), .Q(R4_q), .clr(RESET));
  not not_5 (not_5_out, CLOCK);
  Register #(.width(16)) R5 (.D(DATA), .en(decoder_1_out5), .clk(not_6_out), .Q(R5_q), .clr(RESET));
  not not_6 (not_6_out, CLOCK);
  Register #(.width(16)) R6 (.D(DATA), .en(decoder_1_out6), .clk(not_7_out), .Q(R6_q), .clr(RESET));
  not not_7 (not_7_out, CLOCK);
  Register #(.width(16)) R7 (.D(DATA), .en(decoder_1_out7), .clk(not_8_out), .Q(R7_q), .clr(RESET));
  not not_8 (not_8_out, CLOCK);
  // Probe on R0_q
  // Probe on R1_q
  // Probe on R2_q
  // Probe on R3_q
  // Probe on R4_q
  // Probe on R5_q
  // Probe on R6_q
  // Probe on R7_q
  Multiplexer #(.select(3), .width(16)) multiplexer_1 (
    .in0(R0_q), .in1(R1_q), .in2(R2_q), .in3(R3_q), .in4(R4_q), .in5(R5_q), .in6(R6_q), .in7(R7_q),
    .out(DATA_RA_OUT), .sel(RA_OUT));
  Multiplexer #(.select(3), .width(16)) multiplexer_2 (
    .in0(R0_q), .in1(R1_q), .in2(R2_q), .in3(R3_q), .in4(R4_q), .in5(R5_q), .in6(R6_q), .in7(R7_q),
    .out(DATA_RB_OUT), .sel(RB_OUT));

  // Notes on the sheet:
  //   R0
  //   R1
  //   R2
  //   R3
  //   R4
  //   R5
  //   R6
  //   R7
endmodule

module INSTRUCTION_REG_MAIN (
  input  [15:0] DATA_IN,
  input  ENABLE,
  input  CLOCK,
  input  RESET,
  output [15:0] DATA_OUT
);

  Register #(.trigger("high"), .width(16)) register_1 (
    .D(DATA_IN), .en(ENABLE), .clk(CLOCK), .Q(DATA_OUT), .clr(RESET));

  // Notes on the sheet:
  //   INSTRUCTION REGISTER MAIN 16 bits
endmodule

module INSTRUCTION_REG_EXT (
  input  [15:0] DATA_IN,
  input  ENABLE,
  input  CLOCK,
  input  RESET,
  output [15:0] DATA_OUT
);

  Register #(.trigger("high"), .width(16)) register_1 (
    .D(DATA_IN), .en(ENABLE), .clk(CLOCK), .Q(DATA_OUT), .clr(RESET));

  // Notes on the sheet:
  //   INSTRUCTION REGISTER EXT 16 bits (Used for data : adresses, immediates, offsets)
endmodule

module PROGRAM_COUNTER (
  input  [15:0] PC_DATA,
  input  PC_Load,
  input  CLOCK,
  input  RESET,
  output [15:0] PC_Out
);

  wire [15:0] adder_1_out, multiplexer_1_out;

  Adder #(.width(16)) adder_1 (.a(PC_Out), .b(16'h1), .out(adder_1_out));  // open: cin, cout
  Multiplexer #(.width(16)) multiplexer_1 (.in0(adder_1_out), .in1(PC_DATA), .out(multiplexer_1_out), .sel(PC_Load));
  Register #(.width(16)) register_1 (.D(multiplexer_1_out), .en(1'b1), .clk(CLOCK), .Q(PC_Out), .clr(RESET));
endmodule

module FLAGS_REG (
  input  IN_Z,
  input  IN_N,
  input  IN_C,
  input  IN_O,
  input  ENABLE,
  input  CLOCK,
  input  RESET,
  output [3:0] OUT_DATA
);

  Register #(.width(4)) register_1 (.D({IN_O, IN_C, IN_N, IN_Z}), .en(ENABLE), .clk(CLOCK), .Q(OUT_DATA), .clr(RESET));

  // Notes on the sheet:
  //   FLAGS REGISTER (4bits) (bit 0 : equal to 0, bit 1 : negative, bit 2 : carry, bit 3 : overflow)
endmodule

module CONTROL_UNIT (
  input  [2:0] OpCode,
  input  [3:0] SubOpCode,
  input  [8:0] OpData,
  input  [3:0] FLAGS,
  output [4:0] ALU_Data,
  output RegWrite,
  output [2:0] SrcRB,
  output [2:0] SrcRA,
  output [2:0] DstR,
  output IsNextExt,
  output FlagsWrite,
  output MemWrite,
  output MemToReg,
  output ContainsAddress,
  output PC_Load,
  output SP_POP,
  output SP_CHANGE,
  output JSR,
  output RTS,
  output REG_IS_ADR,
  output HALT,
  output USE_IN,
  output USE_OUT,
  output [1:0] IO_PORT
);

  wire and_1_out, comparator_1_eq, comparator_1_gt, comparator_2_eq, comparator_3_eq, comparator_4_eq,
       comparator_5_eq, comparator_6_eq, comparator_7_eq, comparator_8_eq, comparator_9_gt, comparator_10_lt,
       comparator_11_eq, multiplexer_2_out, multiplexer_3_out, multiplexer_4_out, multiplexer_6_out,
       multiplexer_7_out, multiplexer_8_out, multiplexer_9_out, multiplexer_10_out, multiplexer_11_out,
       multiplexer_12_out, multiplexer_13_out, multiplexer_15_out, multiplexer_19_out, multiplexer_21_out,
       multiplexer_23_out, nor_1_out, not_1_out, not_2_out, not_3_out, or_1_out, or_2_out, or_3_out,
       xnor_1_out, xor_1_out;
  wire [1:0] multiplexer_25_out;
  wire [4:0] multiplexer_1_out, multiplexer_5_out;

  xnor xnor_1 (xnor_1_out, FLAGS[3], FLAGS[1]);
  and and_1 (and_1_out, xnor_1_out, not_1_out);
  not not_1 (not_1_out, FLAGS[0]);
  xor xor_1 (xor_1_out, FLAGS[3], FLAGS[1]);
  or or_1 (or_1_out, FLAGS[0], xor_1_out);
  Multiplexer #(.select(4), .width(5)) multiplexer_1 (
    .in0(5'b10000), .in1(5'b10001), .in2(5'b10010), .in3(5'b10011), .in4(5'b10100), .in5(5'b10101),
    .in6(5'b10110), .in7(5'b10111), .in8(5'b11000), .in9(5'b11001), .in10({5{1'b0}}), .in11({5{1'b0}}),
    .in12({5{1'b0}}), .in13({5{1'b0}}), .in14({5{1'b0}}), .in15({5{1'b0}}), .out(multiplexer_1_out),
    .sel(SubOpCode));
  Multiplexer #(.select(4)) multiplexer_2 (
    .in0(1'b0), .in1(1'b1), .in2(1'b1), .in3(1'b1), .in4(1'b0), .in5(1'b0), .in6(1'b0), .in7(1'b0),
    .in8(1'b0), .in9(1'b0), .in10(1'b0), .in11(1'b0), .in12(1'b0), .in13(1'b0), .in14(1'b0), .in15(1'b0),
    .out(multiplexer_2_out), .sel(SubOpCode));
  nor nor_1 (nor_1_out, FLAGS[2], FLAGS[0]);
  Multiplexer #(.select(4)) multiplexer_3 (
    .in0(1'b1), .in1(1'b1), .in2(1'b0), .in3(1'b0), .in4(1'b0), .in5(1'b0), .in6(1'b0), .in7(1'b0),
    .in8(1'b0), .in9(1'b0), .in10(1'b0), .in11(1'b0), .in12(1'b0), .in13(1'b0), .in14(1'b0), .in15(1'b0),
    .out(multiplexer_3_out), .sel(SubOpCode));
  or or_2 (or_2_out, FLAGS[2], FLAGS[0]);
  not not_2 (not_2_out, FLAGS[2]);
  Multiplexer #(.select(4)) multiplexer_4 (
    .in0(1'b0), .in1(1'b1), .in2(1'b0), .in3(1'b0), .in4(1'b0), .in5(1'b0), .in6(1'b0), .in7(1'b0),
    .in8(1'b0), .in9(1'b0), .in10(1'b0), .in11(1'b0), .in12(1'b0), .in13(1'b0), .in14(1'b0), .in15(1'b0),
    .out(multiplexer_4_out), .sel(SubOpCode));
  Multiplexer #(.select(4), .width(5)) multiplexer_5 (
    .in0({5{1'b0}}), .in1({5{1'b0}}), .in2({5{1'b0}}), .in3({5{1'b0}}), .in4({5{1'b0}}), .in5({5{1'b0}}),
    .in6({5{1'b0}}), .in7({5{1'b0}}), .in8({5{1'b0}}), .in9({5{1'b0}}), .in10(5'b11010), .in11(5'b11011),
    .in12({5{1'b0}}), .in13({5{1'b0}}), .in14({5{1'b0}}), .in15({5{1'b0}}), .out(multiplexer_5_out),
    .sel(SubOpCode));
  Multiplexer #(.select(4)) multiplexer_6 (
    .in0(1'b0), .in1(1'b0), .in2(1'b0), .in3(1'b0), .in4(1'b0), .in5(1'b0), .in6(1'b0), .in7(1'b0),
    .in8(1'b0), .in9(1'b0), .in10(1'b0), .in11(1'b1), .in12(1'b0), .in13(1'b0), .in14(1'b0), .in15(1'b0),
    .out(multiplexer_6_out), .sel(SubOpCode));
  Multiplexer #(.select(4)) multiplexer_7 (
    .in0(1'b1), .in1(1'b0), .in2(1'b0), .in3(1'b1), .in4(1'b0), .in5(1'b0), .in6(1'b0), .in7(1'b0),
    .in8(1'b0), .in9(1'b0), .in10(1'b0), .in11(1'b0), .in12(1'b0), .in13(1'b0), .in14(1'b0), .in15(1'b0),
    .out(multiplexer_7_out), .sel(SubOpCode));
  Multiplexer #(.select(4)) multiplexer_8 (
    .in0(1'b0), .in1(1'b1), .in2(1'b0), .in3(1'b0), .in4(1'b0), .in5(1'b0), .in6(1'b0), .in7(1'b0),
    .in8(1'b0), .in9(1'b0), .in10(1'b0), .in11(1'b0), .in12(1'b0), .in13(1'b0), .in14(1'b0), .in15(1'b0),
    .out(multiplexer_8_out), .sel(SubOpCode));
  Multiplexer #(.select(4)) multiplexer_9 (
    .in0(1'b0), .in1(1'b0), .in2(1'b0), .in3(1'b0), .in4(1'b0), .in5(1'b0), .in6(1'b0), .in7(1'b0),
    .in8(1'b0), .in9(1'b0), .in10(1'b1), .in11(1'b0), .out(multiplexer_9_out), .sel(SubOpCode));  // open: in12, in13, in14, in15
  Multiplexer #(.select(4)) multiplexer_10 (
    .in0(1'b0), .in1(1'b1), .in2(1'b1), .in3(1'b0), .in4(1'b0), .in5(1'b0), .in6(1'b0), .in7(1'b0),
    .in8(1'b0), .in9(1'b0), .in10(1'b0), .in11(1'b0), .in12(1'b0), .in13(1'b0), .in14(1'b0), .in15(1'b0),
    .out(multiplexer_10_out), .sel(SubOpCode));
  Multiplexer #(.select(4)) multiplexer_11 (
    .in0(1'b1), .in1(1'b0), .in2(1'b0), .in3(1'b1), .in4(1'b0), .in5(1'b0), .in6(1'b0), .in7(1'b0),
    .in8(1'b0), .in9(1'b0), .in10(1'b0), .in11(1'b0), .in12(1'b0), .in13(1'b0), .in14(1'b0), .in15(1'b0),
    .out(multiplexer_11_out), .sel(SubOpCode));
  not not_3 (not_3_out, FLAGS[0]);
  Multiplexer #(.select(4)) multiplexer_12 (
    .in0(1'b1), .in1(FLAGS[0]), .in2(not_3_out), .in3(FLAGS[2]), .in4(or_2_out), .in5(nor_1_out),
    .in6(not_2_out), .in7(xor_1_out), .in8(or_1_out), .in9(and_1_out), .in10(xnor_1_out), .in11(1'b1),
    .in12(1'b0), .in13(1'b0), .in14(1'b0), .in15(1'b0), .out(multiplexer_12_out), .sel(SubOpCode));
  Multiplexer #(.select(4)) multiplexer_13 (
    .in0(1'b0), .in1(1'b0), .in2(1'b0), .in3(1'b0), .in4(1'b0), .in5(1'b0), .in6(1'b0), .in7(1'b0),
    .in8(1'b0), .in9(1'b0), .in10(1'b0), .in11(1'b1), .in12(1'b1), .in13(1'b0), .in14(1'b0), .in15(1'b0),
    .out(multiplexer_13_out), .sel(SubOpCode));
  Multiplexer #(.select(3), .width(5)) multiplexer_14 (
    .in0(multiplexer_1_out), .in1(multiplexer_5_out), .in2({5{1'b0}}), .in3({5{1'b0}}), .in4({5{1'b0}}),
    .in5({5{1'b0}}), .in6({5{1'b0}}), .in7({5{1'b0}}), .out(ALU_Data), .sel(OpCode));
  Multiplexer #(.select(4)) multiplexer_15 (
    .in0(1'b0), .in1(1'b1), .in2(1'b0), .in3(1'b0), .in4(1'b0), .in5(1'b0), .in6(1'b0), .in7(1'b0),
    .in8(1'b0), .in9(1'b0), .in10(1'b0), .in11(1'b0), .in12(1'b0), .in13(1'b0), .in14(1'b0), .in15(1'b0),
    .out(multiplexer_15_out), .sel(SubOpCode));
  Multiplexer #(.select(3)) multiplexer_16 (
    .in0(1'b0), .in1(multiplexer_9_out), .in2(1'b0), .in3(1'b0), .in4(1'b0), .in5(1'b0), .in6(1'b0),
    .in7(1'b0), .out(FlagsWrite), .sel(OpCode));
  Multiplexer #(.select(3)) multiplexer_17 (
    .in0(1'b0), .in1(1'b0), .in2(1'b0), .in3(multiplexer_10_out), .in4(1'b0), .in5(1'b0), .in6(1'b0),
    .in7(1'b0), .out(MemWrite), .sel(OpCode));
  Multiplexer #(.select(3)) multiplexer_18 (
    .in0(1'b0), .in1(1'b0), .in2(1'b0), .in3(multiplexer_11_out), .in4(1'b0), .in5(1'b0), .in6(1'b0),
    .in7(1'b0), .out(MemToReg), .sel(OpCode));
  Multiplexer #(.select(4)) multiplexer_19 (
    .in0(1'b0), .in1(1'b0), .in2(1'b0), .in3(1'b0), .in4(1'b0), .in5(1'b0), .in6(1'b0), .in7(1'b0),
    .in8(1'b0), .in9(1'b0), .in10(1'b0), .in11(1'b0), .in12(1'b1), .in13(1'b0), .in14(1'b0), .in15(1'b0),
    .out(multiplexer_19_out), .sel(SubOpCode));
  Comparator #(.width(4)) comparator_1 (
    .a(SubOpCode), .b(4'b0100), .gt(comparator_1_gt), .eq(comparator_1_eq));  // open: lt
  Multiplexer #(.select(3)) multiplexer_20 (
    .in0(1'b1), .in1(multiplexer_6_out), .in2(1'b1), .in3(multiplexer_7_out), .in4(1'b0),
    .in5(multiplexer_8_out), .in6(1'b0), .in7(multiplexer_2_out), .out(RegWrite), .sel(OpCode));
  Comparator #(.width(3)) comparator_2 (.a(OpCode), .b(3'b100), .eq(comparator_2_eq));  // open: gt, lt
  Comparator #(.width(4)) comparator_3 (.a(SubOpCode), .b(4'b1011), .eq(comparator_3_eq));  // open: gt, lt
  Comparator #(.width(3)) comparator_4 (.a(OpCode), .b(3'b100), .eq(comparator_4_eq));  // open: gt, lt
  Comparator #(.width(4)) comparator_5 (.a(SubOpCode), .b(4'b1100), .eq(comparator_5_eq));  // open: gt, lt
  Multiplexer #(.select(4)) multiplexer_21 (
    .in0(1'b0), .in1(1'b0), .in2(1'b1), .in3(1'b1), .in4(1'b0), .in5(1'b0), .in6(1'b0), .in7(1'b0),
    .in8(1'b0), .in9(1'b0), .in10(1'b0), .in11(1'b0), .in12(1'b0), .in13(1'b0), .in14(1'b0), .in15(1'b0),
    .out(multiplexer_21_out), .sel(SubOpCode));
  Comparator #(.width(3)) comparator_6 (.a(OpCode), .b(3'b111), .eq(comparator_6_eq));  // open: gt, lt
  Comparator #(.width(4)) comparator_7 (.a(SubOpCode), .b(4'b0000), .eq(comparator_7_eq));  // open: gt, lt
  Comparator #(.width(3)) comparator_8 (.a(OpCode), .b(3'b111), .eq(comparator_8_eq));  // open: gt, lt
  Comparator #(.width(4)) comparator_9 (.a(SubOpCode), .b(4'b0000), .gt(comparator_9_gt));  // open: eq, lt
  Comparator #(.width(4)) comparator_10 (.a(SubOpCode), .b(4'b0100), .lt(comparator_10_lt));  // open: gt, eq
  Comparator #(.width(3)) comparator_11 (.a(OpCode), .b(3'b111), .eq(comparator_11_eq));  // open: gt, lt
  or or_3 (or_3_out, comparator_1_gt, comparator_1_eq);
  Multiplexer #(.select(3)) multiplexer_22 (
    .in0(1'b0), .in1(1'b0), .in2(1'b1), .in3(multiplexer_3_out), .in4(1'b1), .in5(multiplexer_15_out),
    .in6(1'b0), .in7(1'b0), .out(IsNextExt), .sel(OpCode));
  Multiplexer #(.select(4)) multiplexer_23 (
    .in0(1'b0), .in1(1'b1), .in2(1'b0), .in3(1'b0), .in4(1'b0), .in5(1'b0), .in6(1'b0), .in7(1'b0),
    .in8(1'b0), .in9(1'b0), .in10(1'b0), .in11(1'b0), .in12(1'b0), .in13(1'b0), .in14(1'b0), .in15(1'b0),
    .out(multiplexer_23_out), .sel(SubOpCode));
  Multiplexer #(.select(3)) multiplexer_24 (
    .in0(1'b0), .in1(1'b0), .in2(1'b0), .in3(multiplexer_21_out), .in4(1'b0), .in5(1'b0), .in6(1'b0),
    .in7(1'b0), .out(REG_IS_ADR), .sel(OpCode));
  and and_2 (USE_OUT, comparator_11_eq, or_3_out);
  Multiplexer #(.select(4), .width(2)) multiplexer_25 (
    .in1(2'b00), .in2(2'b01), .in3(2'b10), .in4(2'b00), .in5(2'b01), .in6(2'b10), .out(multiplexer_25_out),
    .sel(SubOpCode));  // open: in0, in7, in8, in9, in10, in11, in12, in13, in14, in15
  Multiplexer #(.select(3)) multiplexer_26 (
    .in0(1'b0), .in1(1'b0), .in2(1'b0), .in3(1'b1), .in4(multiplexer_12_out), .in5(multiplexer_4_out),
    .in6(1'b0), .in7(1'b0), .out(ContainsAddress), .sel(OpCode));
  Multiplexer #(.select(3)) multiplexer_27 (
    .in0(1'b0), .in1(1'b0), .in2(1'b0), .in3(1'b0), .in4(1'b1), .in5(1'b0), .in6(1'b0), .in7(1'b0),
    .out(PC_Load), .sel(OpCode));
  and and_3 (JSR, comparator_2_eq, comparator_3_eq);
  and and_4 (RTS, comparator_4_eq, comparator_5_eq);
  and and_5 (HALT, comparator_6_eq, comparator_7_eq);
  and and_6 (USE_IN, comparator_8_eq, comparator_9_gt, comparator_10_lt);
  Multiplexer #(.select(3)) multiplexer_28 (
    .in0(1'b0), .in1(1'b0), .in2(1'b0), .in3(1'b0), .in4(multiplexer_19_out), .in5(multiplexer_23_out),
    .in6(1'b0), .in7(1'b0), .out(SP_POP), .sel(OpCode));
  Multiplexer #(.select(3)) multiplexer_29 (
    .in0(1'b0), .in1(1'b0), .in2(1'b0), .in3(1'b0), .in4(multiplexer_13_out), .in5(1'b1), .in6(1'b0),
    .in7(1'b0), .out(SP_CHANGE), .sel(OpCode));
  Multiplexer #(.select(3), .width(2)) multiplexer_30 (
    .in7(multiplexer_25_out), .out(IO_PORT), .sel(OpCode));  // open: in0, in1, in2, in3, in4, in5, in6

  assign DstR = OpData[8:6];
  assign SrcRA = OpData[5:3];
  assign SrcRB = OpData[2:0];

  // Notes on the sheet:
  //   ENABLE WRITING TO FLAGS REGISTER
  //   UPPER BIT IS : ENABLE/DISABLE ALU, LOWER 4 BITS ARE : ALUOpSubCode
  //   ENABLE WRITING TO GP REGISTER (DstR)
  //   INDICATES THAT THE NEXT WORD IS AN EXTENSION OF THIS INSTRUCTION
endmodule
